// Logisim project ends-fixture.circ as structural Verilog: 3 circuits, main circuit main
module main (
  input  in_1,
  input  in_2,
  input  in_3,
  input  in_4,
  output [7:0] out_5,
  output [7:0] out_6,
  output [7:0] out_7,
  output [7:0] out_8
);

  // AND_Gate and_1 is placed but not wired
  // AND_Gate and_2 is placed but not wired
  // AND_Gate and_3 is placed but not wired
  // NAND_Gate nand_1 is placed but not wired
  // NAND_Gate nand_2 is placed but not wired
  // NAND_Gate nand_3 is placed but not wired
  // OR_Gate or_1 is placed but not wired
  // OR_Gate or_2 is placed but not wired
  // OR_Gate or_3 is placed but not wired
  // XOR_Gate xor_1 is placed but not wired
  // XOR_Gate xor_2 is placed but not wired
  // XOR_Gate xor_3 is placed but not wired
  // XNOR_Gate xnor_1 is placed but not wired
  // XNOR_Gate xnor_2 is placed but not wired
  // XNOR_Gate xnor_3 is placed but not wired
  // Odd_Parity odd_parity_1 is placed but not wired
  // Odd_Parity odd_parity_2 is placed but not wired
  // Odd_Parity odd_parity_3 is placed but not wired
  // AND_Gate and_4 is placed but not wired
  Controlled_Inverter controlled_inverter_1 ();  // open: in, out, en
  Controlled_Inverter controlled_inverter_2 ();  // open: in, out, en
  Multiplexer #(.select(1), .enable("true")) multiplexer_1 ();  // open: in0, in1, out, sel, en
  Multiplexer #(.select(3), .enable("true")) multiplexer_2 ();  // open: in0, in1, in2, in3, in4, in5, in6, in7, out, sel, en
  Demultiplexer #(.select(2), .enable("true")) demultiplexer_1 ();  // open: out0, out1, out2, out3, in, sel, en
  Demultiplexer #(.select(1), .enable("true")) demultiplexer_2 ();  // open: out0, out1, in, sel, en
  Demultiplexer #(.select(3), .enable("true")) demultiplexer_3 ();  // open: out0, out1, out2, out3, out4, out5, out6, out7, in, sel, en
  Decoder #(.select(2), .enable("true")) decoder_1 ();  // open: out0, out1, out2, out3, sel, en
  Decoder #(.select(1), .enable("true")) decoder_2 ();  // open: out0, out1, sel, en
  BitSelector #(.width(8), .group(3)) bitselector_1 ();  // open: in, out, sel
  LED led_1 ();  // open: in
  LED led_2 ();  // open: in
  Shifter #(.width(3)) shifter_1 ();  // open: in, dist, out
  Hex_Digit_Display hex_digit_display_1 ();  // open: value, dp
  // AND_Gate and_5 is placed but not wired
  // AND_Gate and_6 is placed but not wired
  // AND_Gate and_7 is placed but not wired
  // NAND_Gate nand_4 is placed but not wired
  // NAND_Gate nand_5 is placed but not wired
  // NAND_Gate nand_6 is placed but not wired
  // OR_Gate or_4 is placed but not wired
  // OR_Gate or_5 is placed but not wired
  // OR_Gate or_6 is placed but not wired
  // XOR_Gate xor_4 is placed but not wired
  // XOR_Gate xor_5 is placed but not wired
  // XOR_Gate xor_6 is placed but not wired
  // XNOR_Gate xnor_4 is placed but not wired
  // XNOR_Gate xnor_5 is placed but not wired
  // XNOR_Gate xnor_6 is placed but not wired
  // Odd_Parity odd_parity_4 is placed but not wired
  // Odd_Parity odd_parity_5 is placed but not wired
  // Odd_Parity odd_parity_6 is placed but not wired
  // OR_Gate or_7 is placed but not wired
  // Buffer buffer_1 is placed but not wired
  Controlled_Inverter controlled_inverter_3 ();  // open: in, out, en
  Multiplexer #(.select(1), .enable("false")) multiplexer_3 ();  // open: in0, in1, out, sel
  Multiplexer #(.select(3), .enable("false")) multiplexer_4 ();  // open: in0, in1, in2, in3, in4, in5, in6, in7, out, sel
  Demultiplexer #(.select(2), .enable("false")) demultiplexer_4 ();  // open: out0, out1, out2, out3, in, sel
  Demultiplexer #(.select(1), .enable("false")) demultiplexer_5 ();  // open: out0, out1, in, sel
  Demultiplexer #(.select(3), .enable("false")) demultiplexer_6 ();  // open: out0, out1, out2, out3, out4, out5, out6, out7, in, sel
  Decoder #(.select(2), .enable("false")) decoder_3 ();  // open: out0, out1, out2, out3, sel
  Decoder #(.select(1), .enable("false")) decoder_4 ();  // open: out0, out1, sel
  BitSelector #(.width(31), .group(31)) bitselector_2 ();  // open: in, out, sel
  Button button_1 ();  // open: out
  Button button_2 ();  // open: out
  Shifter #(.width(8)) shifter_2 ();  // open: in, dist, out
  sub sub_1 ();  // open: in_2, in_3, out_4, in_1
  // AND_Gate and_8 is placed but not wired
  // AND_Gate and_9 is placed but not wired
  // AND_Gate and_10 is placed but not wired
  // NAND_Gate nand_7 is placed but not wired
  // NAND_Gate nand_8 is placed but not wired
  // NAND_Gate nand_9 is placed but not wired
  // OR_Gate or_8 is placed but not wired
  // OR_Gate or_9 is placed but not wired
  // OR_Gate or_10 is placed but not wired
  // XOR_Gate xor_7 is placed but not wired
  // XOR_Gate xor_8 is placed but not wired
  // XOR_Gate xor_9 is placed but not wired
  // XNOR_Gate xnor_7 is placed but not wired
  // XNOR_Gate xnor_8 is placed but not wired
  // XNOR_Gate xnor_9 is placed but not wired
  // Odd_Parity odd_parity_7 is placed but not wired
  // Odd_Parity odd_parity_8 is placed but not wired
  // Odd_Parity odd_parity_9 is placed but not wired
  // XNOR_Gate xnor_10 is placed but not wired
  Controlled_Buffer controlled_buffer_1 ();  // open: in, out, en
  // NOT_Gate not_1 is placed but not wired
  Multiplexer #(.select(1), .enable("true")) multiplexer_5 ();  // open: in0, in1, out, sel, en
  Multiplexer #(.select(3), .enable("true")) multiplexer_6 ();  // open: in0, in1, in2, in3, in4, in5, in6, in7, out, sel, en
  Demultiplexer #(.select(2), .enable("true")) demultiplexer_7 ();  // open: out0, out1, out2, out3, in, sel, en
  Demultiplexer #(.select(1), .enable("true")) demultiplexer_8 ();  // open: out0, out1, in, sel, en
  Demultiplexer #(.select(3), .enable("true")) demultiplexer_9 ();  // open: out0, out1, out2, out3, out4, out5, out6, out7, in, sel, en
  Decoder #(.select(2), .enable("true")) decoder_5 ();  // open: out0, out1, out2, out3, sel, en
  Decoder #(.select(1), .enable("true")) decoder_6 ();  // open: out0, out1, sel, en
  // Priority_Encoder #(.select(1)) priority_encoder_1: pin names not known
  Shifter #(.width(32)) shifter_3 ();  // open: in, dist, out
  plain plain_1 ();  // open: in_3, in_4, in_5, in_1, in_2, out_7, out_6
  // AND_Gate and_11 is placed but not wired
  // AND_Gate and_12 is placed but not wired
  // AND_Gate and_13 is placed but not wired
  // NAND_Gate nand_10 is placed but not wired
  // NAND_Gate nand_11 is placed but not wired
  // NAND_Gate nand_12 is placed but not wired
  // OR_Gate or_11 is placed but not wired
  // OR_Gate or_12 is placed but not wired
  // OR_Gate or_13 is placed but not wired
  // XOR_Gate xor_10 is placed but not wired
  // XOR_Gate xor_11 is placed but not wired
  // XOR_Gate xor_12 is placed but not wired
  // XNOR_Gate xnor_11 is placed but not wired
  // XNOR_Gate xnor_12 is placed but not wired
  // XNOR_Gate xnor_13 is placed but not wired
  // Odd_Parity odd_parity_10 is placed but not wired
  // Odd_Parity odd_parity_11 is placed but not wired
  // Odd_Parity odd_parity_12 is placed but not wired
  // NOT_Gate not_2 is placed but not wired
  Controlled_Buffer controlled_buffer_2 ();  // open: in, out, en
  Controlled_Inverter controlled_inverter_4 ();  // open: in, out, en
  Multiplexer #(.select(1), .enable("false")) multiplexer_7 ();  // open: in0, in1, out, sel
  Multiplexer #(.select(3), .enable("false")) multiplexer_8 ();  // open: in0, in1, in2, in3, in4, in5, in6, in7, out, sel
  Demultiplexer #(.select(2), .enable("false")) demultiplexer_10 ();  // open: out0, out1, out2, out3, in, sel
  Demultiplexer #(.select(1), .enable("false")) demultiplexer_11 ();  // open: out0, out1, in, sel
  Demultiplexer #(.select(3), .enable("false")) demultiplexer_12 ();  // open: out0, out1, out2, out3, out4, out5, out6, out7, in, sel
  Decoder #(.select(2), .enable("false")) decoder_7 ();  // open: out0, out1, out2, out3, sel
  Decoder #(.select(1), .enable("false")) decoder_8 ();  // open: out0, out1, sel
  // Priority_Encoder #(.select(2)) priority_encoder_2: pin names not known
  BitAdder #(.width(8)) bitadder_1 ();  // open: in0, out
  sub sub_2 ();  // open: in_2, in_3, out_4, in_1
  // AND_Gate and_14 is placed but not wired
  // AND_Gate and_15 is placed but not wired
  // AND_Gate and_16 is placed but not wired
  // NAND_Gate nand_13 is placed but not wired
  // NAND_Gate nand_14 is placed but not wired
  // NAND_Gate nand_15 is placed but not wired
  // OR_Gate or_14 is placed but not wired
  // OR_Gate or_15 is placed but not wired
  // OR_Gate or_16 is placed but not wired
  // XOR_Gate xor_13 is placed but not wired
  // XOR_Gate xor_14 is placed but not wired
  // XOR_Gate xor_15 is placed but not wired
  // XNOR_Gate xnor_14 is placed but not wired
  // XNOR_Gate xnor_15 is placed but not wired
  // XNOR_Gate xnor_16 is placed but not wired
  // Odd_Parity odd_parity_13 is placed but not wired
  // Odd_Parity odd_parity_14 is placed but not wired
  // Odd_Parity odd_parity_15 is placed but not wired
  Controlled_Inverter controlled_inverter_5 ();  // open: in, out, en
  // AND_Gate and_17 is placed but not wired
  Controlled_Inverter controlled_inverter_6 ();  // open: in, out, en
  Multiplexer #(.select(2), .enable("true")) multiplexer_9 ();  // open: in0, in1, in2, in3, out, sel, en
  Multiplexer #(.select(1), .enable("true")) multiplexer_10 ();  // open: in0, in1, out, sel, en
  Demultiplexer #(.select(3), .enable("true")) demultiplexer_13 ();  // open: out0, out1, out2, out3, out4, out5, out6, out7, in, sel, en
  Demultiplexer #(.select(2), .enable("true")) demultiplexer_14 ();  // open: out0, out1, out2, out3, in, sel, en
  Decoder #(.select(1), .enable("true")) decoder_9 ();  // open: out0, out1, sel, en
  Decoder #(.select(3), .enable("true")) decoder_10 ();  // open: out0, out1, out2, out3, out4, out5, out6, out7, sel, en
  Decoder #(.select(2), .enable("true")) decoder_11 ();  // open: out0, out1, out2, out3, sel, en
  // Priority_Encoder #(.select(3)) priority_encoder_3: pin names not known
  BitAdder #(.width(8)) bitadder_2 ();  // open: in0, in1, out
  plain plain_2 ();  // open: in_3, in_4, in_5, in_1, in_2, out_7, out_6
  // AND_Gate and_18 is placed but not wired
  // AND_Gate and_19 is placed but not wired
  // AND_Gate and_20 is placed but not wired
  // NAND_Gate nand_16 is placed but not wired
  // NAND_Gate nand_17 is placed but not wired
  // NAND_Gate nand_18 is placed but not wired
  // OR_Gate or_17 is placed but not wired
  // OR_Gate or_18 is placed but not wired
  // OR_Gate or_19 is placed but not wired
  // XOR_Gate xor_16 is placed but not wired
  // XOR_Gate xor_17 is placed but not wired
  // XOR_Gate xor_18 is placed but not wired
  // XNOR_Gate xnor_17 is placed but not wired
  // XNOR_Gate xnor_18 is placed but not wired
  // XNOR_Gate xnor_19 is placed but not wired
  // Odd_Parity odd_parity_16 is placed but not wired
  // Odd_Parity odd_parity_17 is placed but not wired
  // Odd_Parity odd_parity_18 is placed but not wired
  Controlled_Inverter controlled_inverter_7 ();  // open: in, out, en
  // OR_Gate or_20 is placed but not wired
  // Buffer buffer_2 is placed but not wired
  Multiplexer #(.select(2), .enable("false")) multiplexer_11 ();  // open: in0, in1, in2, in3, out, sel
  Multiplexer #(.select(1), .enable("false")) multiplexer_12 ();  // open: in0, in1, out, sel
  Demultiplexer #(.select(3), .enable("false")) demultiplexer_15 ();  // open: out0, out1, out2, out3, out4, out5, out6, out7, in, sel
  Demultiplexer #(.select(2), .enable("false")) demultiplexer_16 ();  // open: out0, out1, out2, out3, in, sel
  Decoder #(.select(1), .enable("false")) decoder_12 ();  // open: out0, out1, sel
  Decoder #(.select(3), .enable("false")) decoder_13 ();  // open: out0, out1, out2, out3, out4, out5, out6, out7, sel
  Decoder #(.select(2), .enable("false")) decoder_14 ();  // open: out0, out1, out2, out3, sel
  BitSelector #(.width(8), .group(3)) bitselector_3 ();  // open: in, out, sel
  // Probe on nothing
  // Probe on nothing
  BitAdder #(.width(8)) bitadder_3 ();  // open: in0, in1, in2, out
  sub sub_3 ();  // open: in_2, in_3, out_4, in_1
  // AND_Gate and_21 is placed but not wired
  // AND_Gate and_22 is placed but not wired
  // AND_Gate and_23 is placed but not wired
  // NAND_Gate nand_19 is placed but not wired
  // NAND_Gate nand_20 is placed but not wired
  // NAND_Gate nand_21 is placed but not wired
  // OR_Gate or_21 is placed but not wired
  // OR_Gate or_22 is placed but not wired
  // OR_Gate or_23 is placed but not wired
  // XOR_Gate xor_19 is placed but not wired
  // XOR_Gate xor_20 is placed but not wired
  // XOR_Gate xor_21 is placed but not wired
  // XNOR_Gate xnor_20 is placed but not wired
  // XNOR_Gate xnor_21 is placed but not wired
  // XNOR_Gate xnor_22 is placed but not wired
  // Odd_Parity odd_parity_19 is placed but not wired
  // Odd_Parity odd_parity_20 is placed but not wired
  // Odd_Parity odd_parity_21 is placed but not wired
  // NOT_Gate not_3 is placed but not wired
  // XNOR_Gate xnor_23 is placed but not wired
  Controlled_Buffer controlled_buffer_3 ();  // open: in, out, en
  Multiplexer #(.select(2), .enable("true")) multiplexer_13 ();  // open: in0, in1, in2, in3, out, sel, en
  Multiplexer #(.select(1), .enable("true")) multiplexer_14 ();  // open: in0, in1, out, sel, en
  Demultiplexer #(.select(3), .enable("true")) demultiplexer_17 ();  // open: out0, out1, out2, out3, out4, out5, out6, out7, in, sel, en
  Demultiplexer #(.select(2), .enable("true")) demultiplexer_18 ();  // open: out0, out1, out2, out3, in, sel, en
  Decoder #(.select(1), .enable("true")) decoder_15 ();  // open: out0, out1, sel, en
  Decoder #(.select(3), .enable("true")) decoder_16 ();  // open: out0, out1, out2, out3, out4, out5, out6, out7, sel, en
  Decoder #(.select(2), .enable("true")) decoder_17 ();  // open: out0, out1, out2, out3, sel, en
  BitSelector #(.width(31), .group(31)) bitselector_4 ();  // open: in, out, sel
  BitAdder #(.width(8)) bitadder_4 ();  // open: in0, in1, in2, in3, out
  plain plain_3 ();  // open: in_3, in_4, in_5, in_1, in_2, out_7, out_6
  // AND_Gate and_24 is placed but not wired
  // AND_Gate and_25 is placed but not wired
  // AND_Gate and_26 is placed but not wired
  // NAND_Gate nand_22 is placed but not wired
  // NAND_Gate nand_23 is placed but not wired
  // NAND_Gate nand_24 is placed but not wired
  // OR_Gate or_24 is placed but not wired
  // OR_Gate or_25 is placed but not wired
  // OR_Gate or_26 is placed but not wired
  // XOR_Gate xor_22 is placed but not wired
  // XOR_Gate xor_23 is placed but not wired
  // XOR_Gate xor_24 is placed but not wired
  // XNOR_Gate xnor_24 is placed but not wired
  // XNOR_Gate xnor_25 is placed but not wired
  // XNOR_Gate xnor_26 is placed but not wired
  // Odd_Parity odd_parity_22 is placed but not wired
  // Odd_Parity odd_parity_23 is placed but not wired
  // Odd_Parity odd_parity_24 is placed but not wired
  Controlled_Inverter controlled_inverter_8 ();  // open: in, out, en
  // NOT_Gate not_4 is placed but not wired
  Controlled_Buffer controlled_buffer_4 ();  // open: in, out, en
  Multiplexer #(.select(2), .enable("false")) multiplexer_15 ();  // open: in0, in1, in2, in3, out, sel
  Multiplexer #(.select(1), .enable("false")) multiplexer_16 ();  // open: in0, in1, out, sel
  Demultiplexer #(.select(3), .enable("false")) demultiplexer_19 ();  // open: out0, out1, out2, out3, out4, out5, out6, out7, in, sel
  Demultiplexer #(.select(2), .enable("false")) demultiplexer_20 ();  // open: out0, out1, out2, out3, in, sel
  Decoder #(.select(1), .enable("false")) decoder_18 ();  // open: out0, out1, sel
  Decoder #(.select(3), .enable("false")) decoder_19 ();  // open: out0, out1, out2, out3, out4, out5, out6, out7, sel
  Decoder #(.select(2), .enable("false")) decoder_20 ();  // open: out0, out1, out2, out3, sel
  Priority_Encoder #(.select(1)) priority_encoder_4 ();  // open: in0, in1, out
  Clock clock_1 ();  // open: out
  Clock clock_2 ();  // open: out
  BitAdder #(.width(8)) bitadder_5 ();  // open: in0, in1, in2, in3, in4, out
  sub sub_4 ();  // open: in_2, in_3, out_4, in_1
  // AND_Gate and_27 is placed but not wired
  // AND_Gate and_28 is placed but not wired
  // AND_Gate and_29 is placed but not wired
  // NAND_Gate nand_25 is placed but not wired
  // NAND_Gate nand_26 is placed but not wired
  // NAND_Gate nand_27 is placed but not wired
  // OR_Gate or_27 is placed but not wired
  // OR_Gate or_28 is placed but not wired
  // OR_Gate or_29 is placed but not wired
  // XOR_Gate xor_25 is placed but not wired
  // XOR_Gate xor_26 is placed but not wired
  // XOR_Gate xor_27 is placed but not wired
  // XNOR_Gate xnor_27 is placed but not wired
  // XNOR_Gate xnor_28 is placed but not wired
  // XNOR_Gate xnor_29 is placed but not wired
  // Odd_Parity odd_parity_25 is placed but not wired
  // Odd_Parity odd_parity_26 is placed but not wired
  // Odd_Parity odd_parity_27 is placed but not wired
  Controlled_Inverter controlled_inverter_9 ();  // open: in, out, en
  Controlled_Inverter controlled_inverter_10 ();  // open: in, out, en
  Multiplexer #(.select(1), .enable("true")) multiplexer_17 ();  // open: in0, in1, out, sel, en
  Multiplexer #(.select(3), .enable("true")) multiplexer_18 ();  // open: in0, in1, in2, in3, in4, in5, in6, in7, out, sel, en
  Multiplexer #(.select(2), .enable("true")) multiplexer_19 ();  // open: in0, in1, in2, in3, out, sel, en
  Demultiplexer #(.select(1), .enable("true")) demultiplexer_21 ();  // open: out0, out1, in, sel, en
  Demultiplexer #(.select(3), .enable("true")) demultiplexer_22 ();  // open: out0, out1, out2, out3, out4, out5, out6, out7, in, sel, en
  Decoder #(.select(2), .enable("true")) decoder_21 ();  // open: out0, out1, out2, out3, sel, en
  Decoder #(.select(1), .enable("true")) decoder_22 ();  // open: out0, out1, sel, en
  Decoder #(.select(3), .enable("true")) decoder_23 ();  // open: out0, out1, out2, out3, out4, out5, out6, out7, sel, en
  Priority_Encoder #(.select(2)) priority_encoder_5 ();  // open: in0, in1, in2, in3, out
  D_Flip_Flop d_ff_1 ();  // open: clk, D, Q, Qn, preset, en, reset
  plain plain_4 ();  // open: in_3, in_4, in_5, in_1, in_2, out_7, out_6
  // AND_Gate and_30 is placed but not wired
  // AND_Gate and_31 is placed but not wired
  // AND_Gate and_32 is placed but not wired
  // NAND_Gate nand_28 is placed but not wired
  // NAND_Gate nand_29 is placed but not wired
  // NAND_Gate nand_30 is placed but not wired
  // OR_Gate or_30 is placed but not wired
  // OR_Gate or_31 is placed but not wired
  // OR_Gate or_32 is placed but not wired
  // XOR_Gate xor_28 is placed but not wired
  // XOR_Gate xor_29 is placed but not wired
  // XOR_Gate xor_30 is placed but not wired
  // XNOR_Gate xnor_30 is placed but not wired
  // XNOR_Gate xnor_31 is placed but not wired
  // XNOR_Gate xnor_32 is placed but not wired
  // Odd_Parity odd_parity_28 is placed but not wired
  // Odd_Parity odd_parity_29 is placed but not wired
  // Odd_Parity odd_parity_30 is placed but not wired
  // Buffer buffer_3 is placed but not wired
  Controlled_Inverter controlled_inverter_11 ();  // open: in, out, en
  Multiplexer #(.select(1), .enable("false")) multiplexer_20 ();  // open: in0, in1, out, sel
  Multiplexer #(.select(3), .enable("false")) multiplexer_21 ();  // open: in0, in1, in2, in3, in4, in5, in6, in7, out, sel
  Multiplexer #(.select(2), .enable("false")) multiplexer_22 ();  // open: in0, in1, in2, in3, out, sel
  Demultiplexer #(.select(1), .enable("false")) demultiplexer_23 ();  // open: out0, out1, in, sel
  Demultiplexer #(.select(3), .enable("false")) demultiplexer_24 ();  // open: out0, out1, out2, out3, out4, out5, out6, out7, in, sel
  Decoder #(.select(2), .enable("false")) decoder_24 ();  // open: out0, out1, out2, out3, sel
  Decoder #(.select(1), .enable("false")) decoder_25 ();  // open: out0, out1, sel
  Decoder #(.select(3), .enable("false")) decoder_26 ();  // open: out0, out1, out2, out3, out4, out5, out6, out7, sel
  Priority_Encoder #(.select(3)) priority_encoder_6 ();  // open: in0, in1, in2, in3, in4, in5, in6, in7, out, en_in
  T_Flip_Flop t_ff_1 ();  // open: clk, T, Q, Qn, preset, reset, en
  // AND_Gate and_33 is placed but not wired
  // AND_Gate and_34 is placed but not wired
  // AND_Gate and_35 is placed but not wired
  // NAND_Gate nand_31 is placed but not wired
  // NAND_Gate nand_32 is placed but not wired
  // NAND_Gate nand_33 is placed but not wired
  // OR_Gate or_33 is placed but not wired
  // OR_Gate or_34 is placed but not wired
  // OR_Gate or_35 is placed but not wired
  // XOR_Gate xor_31 is placed but not wired
  // XOR_Gate xor_32 is placed but not wired
  // XOR_Gate xor_33 is placed but not wired
  // XNOR_Gate xnor_33 is placed but not wired
  // XNOR_Gate xnor_34 is placed but not wired
  // XNOR_Gate xnor_35 is placed but not wired
  // Odd_Parity odd_parity_31 is placed but not wired
  // Odd_Parity odd_parity_32 is placed but not wired
  // Odd_Parity odd_parity_33 is placed but not wired
  Controlled_Buffer controlled_buffer_5 ();  // open: in, out, en
  // NOT_Gate not_5 is placed but not wired
  Multiplexer #(.select(1), .enable("true")) multiplexer_23 ();  // open: in0, in1, out, sel, en
  Multiplexer #(.select(3), .enable("true")) multiplexer_24 ();  // open: in0, in1, in2, in3, in4, in5, in6, in7, out, sel, en
  Multiplexer #(.select(2), .enable("true")) multiplexer_25 ();  // open: in0, in1, in2, in3, out, sel, en
  Demultiplexer #(.select(1), .enable("true")) demultiplexer_25 ();  // open: out0, out1, in, sel, en
  Demultiplexer #(.select(3), .enable("true")) demultiplexer_26 ();  // open: out0, out1, out2, out3, out4, out5, out6, out7, in, sel, en
  Decoder #(.select(2), .enable("true")) decoder_27 ();  // open: out0, out1, out2, out3, sel, en
  Decoder #(.select(1), .enable("true")) decoder_28 ();  // open: out0, out1, sel, en
  Decoder #(.select(3), .enable("true")) decoder_29 ();  // open: out0, out1, out2, out3, out4, out5, out6, out7, sel, en
  BitSelector #(.width(8), .group(3)) bitselector_5 ();  // open: in, out, sel
  LED led_3 ();  // open: in
  LED led_4 ();  // open: in
  J_K_Flip_Flop j_k_ff_1 ();  // open: J, clk, K, Q, Qn, preset, en, reset
  // AND_Gate and_36 is placed but not wired
  // AND_Gate and_37 is placed but not wired
  // AND_Gate and_38 is placed but not wired
  // NAND_Gate nand_34 is placed but not wired
  // NAND_Gate nand_35 is placed but not wired
  // NAND_Gate nand_36 is placed but not wired
  // OR_Gate or_36 is placed but not wired
  // OR_Gate or_37 is placed but not wired
  // OR_Gate or_38 is placed but not wired
  // XOR_Gate xor_34 is placed but not wired
  // XOR_Gate xor_35 is placed but not wired
  // XOR_Gate xor_36 is placed but not wired
  // XNOR_Gate xnor_36 is placed but not wired
  // XNOR_Gate xnor_37 is placed but not wired
  // XNOR_Gate xnor_38 is placed but not wired
  // Odd_Parity odd_parity_34 is placed but not wired
  // Odd_Parity odd_parity_35 is placed but not wired
  // Odd_Parity odd_parity_36 is placed but not wired
  Controlled_Buffer controlled_buffer_6 ();  // open: in, out, en
  Controlled_Inverter controlled_inverter_12 ();  // open: in, out, en
  Multiplexer #(.select(1), .enable("false")) multiplexer_26 ();  // open: in0, in1, out, sel
  Multiplexer #(.select(3), .enable("false")) multiplexer_27 ();  // open: in0, in1, in2, in3, in4, in5, in6, in7, out, sel
  Multiplexer #(.select(2), .enable("false")) multiplexer_28 ();  // open: in0, in1, in2, in3, out, sel
  Demultiplexer #(.select(1), .enable("false")) demultiplexer_27 ();  // open: out0, out1, in, sel
  Demultiplexer #(.select(3), .enable("false")) demultiplexer_28 ();  // open: out0, out1, out2, out3, out4, out5, out6, out7, in, sel
  Decoder #(.select(2), .enable("false")) decoder_30 ();  // open: out0, out1, out2, out3, sel
  Decoder #(.select(1), .enable("false")) decoder_31 ();  // open: out0, out1, sel
  Decoder #(.select(3), .enable("false")) decoder_32 ();  // open: out0, out1, out2, out3, out4, out5, out6, out7, sel
  BitSelector #(.width(31), .group(31)) bitselector_6 ();  // open: in, out, sel
  Button button_3 ();  // open: out
  Button button_4 ();  // open: out
  S_R_Flip_Flop s_r_ff_1 ();  // open: S, clk, R, Q, Qn, preset, reset, en
  // AND_Gate and_39 is placed but not wired
  // AND_Gate and_40 is placed but not wired
  // AND_Gate and_41 is placed but not wired
  // NAND_Gate nand_37 is placed but not wired
  // NAND_Gate nand_38 is placed but not wired
  // NAND_Gate nand_39 is placed but not wired
  // OR_Gate or_39 is placed but not wired
  // OR_Gate or_40 is placed but not wired
  // OR_Gate or_41 is placed but not wired
  // XOR_Gate xor_37 is placed but not wired
  // XOR_Gate xor_38 is placed but not wired
  // XOR_Gate xor_39 is placed but not wired
  // XNOR_Gate xnor_39 is placed but not wired
  // XNOR_Gate xnor_40 is placed but not wired
  // XNOR_Gate xnor_41 is placed but not wired
  // Odd_Parity odd_parity_37 is placed but not wired
  // Odd_Parity odd_parity_38 is placed but not wired
  // Odd_Parity odd_parity_39 is placed but not wired
  // AND_Gate and_42 is placed but not wired
  Controlled_Inverter controlled_inverter_13 ();  // open: in, out, en
  Multiplexer #(.select(2), .enable("true")) multiplexer_29 ();  // open: in0, in1, in2, in3, out, sel, en
  Multiplexer #(.select(1), .enable("true")) multiplexer_30 ();  // open: in0, in1, out, sel, en
  Multiplexer #(.select(3), .enable("true")) multiplexer_31 ();  // open: in0, in1, in2, in3, in4, in5, in6, in7, out, sel, en
  Demultiplexer #(.select(2), .enable("true")) demultiplexer_29 ();  // open: out0, out1, out2, out3, in, sel, en
  Demultiplexer #(.select(1), .enable("true")) demultiplexer_30 ();  // open: out0, out1, in, sel, en
  Decoder #(.select(3), .enable("true")) decoder_33 ();  // open: out0, out1, out2, out3, out4, out5, out6, out7, sel, en
  Decoder #(.select(2), .enable("true")) decoder_34 ();  // open: out0, out1, out2, out3, sel, en
  Priority_Encoder #(.select(1)) priority_encoder_7 ();  // open: in0, in1, out, gs, en_out, en_in
  Bit_Extender #(.\type ("zero"), .in_width(4), .out_width(8)) bit_extender_1 ();  // open: in, out
  Register register_1 ();  // open: D, en, Q, clk, clr
  // AND_Gate and_43 is placed but not wired
  // AND_Gate and_44 is placed but not wired
  // AND_Gate and_45 is placed but not wired
  // NAND_Gate nand_40 is placed but not wired
  // NAND_Gate nand_41 is placed but not wired
  // NAND_Gate nand_42 is placed but not wired
  // OR_Gate or_42 is placed but not wired
  // OR_Gate or_43 is placed but not wired
  // OR_Gate or_44 is placed but not wired
  // XOR_Gate xor_40 is placed but not wired
  // XOR_Gate xor_41 is placed but not wired
  // XOR_Gate xor_42 is placed but not wired
  // XNOR_Gate xnor_42 is placed but not wired
  // XNOR_Gate xnor_43 is placed but not wired
  // XNOR_Gate xnor_44 is placed but not wired
  // Odd_Parity odd_parity_40 is placed but not wired
  // Odd_Parity odd_parity_41 is placed but not wired
  // Odd_Parity odd_parity_42 is placed but not wired
  // OR_Gate or_45 is placed but not wired
  // Buffer buffer_4 is placed but not wired
  Multiplexer #(.select(2), .enable("false")) multiplexer_32 ();  // open: in0, in1, in2, in3, out, sel
  Multiplexer #(.select(1), .enable("false")) multiplexer_33 ();  // open: in0, in1, out, sel
  Multiplexer #(.select(3), .enable("false")) multiplexer_34 ();  // open: in0, in1, in2, in3, in4, in5, in6, in7, out, sel
  Demultiplexer #(.select(2), .enable("false")) demultiplexer_31 ();  // open: out0, out1, out2, out3, in, sel
  Demultiplexer #(.select(1), .enable("false")) demultiplexer_32 ();  // open: out0, out1, in, sel
  Decoder #(.select(3), .enable("false")) decoder_35 ();  // open: out0, out1, out2, out3, out4, out5, out6, out7, sel
  Decoder #(.select(2), .enable("false")) decoder_36 ();  // open: out0, out1, out2, out3, sel
  Priority_Encoder #(.select(2)) priority_encoder_8 ();  // open: in0, in1, in2, in3, out, gs, en_out, en_in
  Bit_Extender #(.\type ("input")) bit_extender_2 ();  // open: in, out, extend
  Counter counter_1 ();  // open: load, D, count, Q, carry, clk, clr
  // AND_Gate and_46 is placed but not wired
  // AND_Gate and_47 is placed but not wired
  // AND_Gate and_48 is placed but not wired
  // NAND_Gate nand_43 is placed but not wired
  // NAND_Gate nand_44 is placed but not wired
  // NAND_Gate nand_45 is placed but not wired
  // OR_Gate or_46 is placed but not wired
  // OR_Gate or_47 is placed but not wired
  // OR_Gate or_48 is placed but not wired
  // XOR_Gate xor_43 is placed but not wired
  // XOR_Gate xor_44 is placed but not wired
  // XOR_Gate xor_45 is placed but not wired
  // XNOR_Gate xnor_45 is placed but not wired
  // XNOR_Gate xnor_46 is placed but not wired
  // XNOR_Gate xnor_47 is placed but not wired
  // Odd_Parity odd_parity_43 is placed but not wired
  // Odd_Parity odd_parity_44 is placed but not wired
  // Odd_Parity odd_parity_45 is placed but not wired
  // XNOR_Gate xnor_48 is placed but not wired
  Controlled_Buffer controlled_buffer_7 ();  // open: in, out, en
  Multiplexer #(.select(2), .enable("true")) multiplexer_35 ();  // open: in0, in1, in2, in3, out, sel, en
  Multiplexer #(.select(1), .enable("true")) multiplexer_36 ();  // open: in0, in1, out, sel, en
  Multiplexer #(.select(3), .enable("true")) multiplexer_37 ();  // open: in0, in1, in2, in3, in4, in5, in6, in7, out, sel, en
  Demultiplexer #(.select(2), .enable("true")) demultiplexer_33 ();  // open: out0, out1, out2, out3, in, sel, en
  Demultiplexer #(.select(1), .enable("true")) demultiplexer_34 ();  // open: out0, out1, in, sel, en
  Decoder #(.select(3), .enable("true")) decoder_37 ();  // open: out0, out1, out2, out3, out4, out5, out6, out7, sel, en
  Decoder #(.select(2), .enable("true")) decoder_38 ();  // open: out0, out1, out2, out3, sel, en
  Priority_Encoder #(.select(3)) priority_encoder_9 ();  // open: in0, in1, in2, in3, in4, in5, in6, in7, out, en_in, gs, en_out
  Adder #(.width(8)) adder_1 ();  // open: a, b, out, cin, cout
  ROM rom_1 ();  // open: addr, data, sel
  // AND_Gate and_49 is placed but not wired
  // AND_Gate and_50 is placed but not wired
  // AND_Gate and_51 is placed but not wired
  // NAND_Gate nand_46 is placed but not wired
  // NAND_Gate nand_47 is placed but not wired
  // NAND_Gate nand_48 is placed but not wired
  // OR_Gate or_49 is placed but not wired
  // OR_Gate or_50 is placed but not wired
  // OR_Gate or_51 is placed but not wired
  // XOR_Gate xor_46 is placed but not wired
  // XOR_Gate xor_47 is placed but not wired
  // XOR_Gate xor_48 is placed but not wired
  // XNOR_Gate xnor_49 is placed but not wired
  // XNOR_Gate xnor_50 is placed but not wired
  // XNOR_Gate xnor_51 is placed but not wired
  // Odd_Parity odd_parity_46 is placed but not wired
  // Odd_Parity odd_parity_47 is placed but not wired
  // Odd_Parity odd_parity_48 is placed but not wired
  // NOT_Gate not_6 is placed but not wired
  Controlled_Buffer controlled_buffer_8 ();  // open: in, out, en
  Multiplexer #(.select(2), .enable("false")) multiplexer_38 ();  // open: in0, in1, in2, in3, out, sel
  Multiplexer #(.select(1), .enable("false")) multiplexer_39 ();  // open: in0, in1, out, sel
  Multiplexer #(.select(3), .enable("false")) multiplexer_40 ();  // open: in0, in1, in2, in3, in4, in5, in6, in7, out, sel
  Demultiplexer #(.select(2), .enable("false")) demultiplexer_35 ();  // open: out0, out1, out2, out3, in, sel
  Demultiplexer #(.select(1), .enable("false")) demultiplexer_36 ();  // open: out0, out1, in, sel
  Decoder #(.select(3), .enable("false")) decoder_39 ();  // open: out0, out1, out2, out3, out4, out5, out6, out7, sel
  Decoder #(.select(2), .enable("false")) decoder_40 ();  // open: out0, out1, out2, out3, sel
  BitSelector #(.width(8), .group(3)) bitselector_7 ();  // open: in, out, sel
  // Probe on nothing
  // Probe on nothing
  Subtractor #(.width(8)) subtractor_1 ();  // open: a, b, out, bin, bout
  RAM #(.bus("separate"), .addrWidth(5), .dataWidth(32)) ram_1 ();  // open: addr, din, data, str, sel, clk, ld, clr
  // AND_Gate and_52 is placed but not wired
  // AND_Gate and_53 is placed but not wired
  // AND_Gate and_54 is placed but not wired
  // NAND_Gate nand_49 is placed but not wired
  // NAND_Gate nand_50 is placed but not wired
  // NAND_Gate nand_51 is placed but not wired
  // OR_Gate or_52 is placed but not wired
  // OR_Gate or_53 is placed but not wired
  // OR_Gate or_54 is placed but not wired
  // XOR_Gate xor_49 is placed but not wired
  // XOR_Gate xor_50 is placed but not wired
  // XOR_Gate xor_51 is placed but not wired
  // XNOR_Gate xnor_52 is placed but not wired
  // XNOR_Gate xnor_53 is placed but not wired
  // XNOR_Gate xnor_54 is placed but not wired
  // Odd_Parity odd_parity_49 is placed but not wired
  // Odd_Parity odd_parity_50 is placed but not wired
  // Odd_Parity odd_parity_51 is placed but not wired
  Controlled_Inverter controlled_inverter_14 ();  // open: in, out, en
  // AND_Gate and_55 is placed but not wired
  Multiplexer #(.select(3), .enable("true")) multiplexer_41 ();  // open: in0, in1, in2, in3, in4, in5, in6, in7, out, sel, en
  Multiplexer #(.select(2), .enable("true")) multiplexer_42 ();  // open: in0, in1, in2, in3, out, sel, en
  Demultiplexer #(.select(1), .enable("true")) demultiplexer_37 ();  // open: out0, out1, in, sel, en
  Demultiplexer #(.select(3), .enable("true")) demultiplexer_38 ();  // open: out0, out1, out2, out3, out4, out5, out6, out7, in, sel, en
  Demultiplexer #(.select(2), .enable("true")) demultiplexer_39 ();  // open: out0, out1, out2, out3, in, sel, en
  Decoder #(.select(1), .enable("true")) decoder_41 ();  // open: out0, out1, sel, en
  Decoder #(.select(3), .enable("true")) decoder_42 ();  // open: out0, out1, out2, out3, out4, out5, out6, out7, sel, en
  BitSelector #(.width(31), .group(31)) bitselector_8 ();  // open: in, out, sel
  Multiplier #(.width(8)) multiplier_1 ();  // open: a, b, out, cin, cout
  RAM #(.bus("combined"), .addrWidth(5), .dataWidth(32)) ram_2 ();  // open: addr, data, sel, clk, ld, clr
  // AND_Gate and_56 is placed but not wired
  // AND_Gate and_57 is placed but not wired
  // AND_Gate and_58 is placed but not wired
  // NAND_Gate nand_52 is placed but not wired
  // NAND_Gate nand_53 is placed but not wired
  // NAND_Gate nand_54 is placed but not wired
  // OR_Gate or_55 is placed but not wired
  // OR_Gate or_56 is placed but not wired
  // OR_Gate or_57 is placed but not wired
  // XOR_Gate xor_52 is placed but not wired
  // XOR_Gate xor_53 is placed but not wired
  // XOR_Gate xor_54 is placed but not wired
  // XNOR_Gate xnor_55 is placed but not wired
  // XNOR_Gate xnor_56 is placed but not wired
  // XNOR_Gate xnor_57 is placed but not wired
  // Odd_Parity odd_parity_52 is placed but not wired
  // Odd_Parity odd_parity_53 is placed but not wired
  // Odd_Parity odd_parity_54 is placed but not wired
  Controlled_Inverter controlled_inverter_15 ();  // open: in, out, en
  // OR_Gate or_58 is placed but not wired
  Multiplexer #(.select(3), .enable("false")) multiplexer_43 ();  // open: in0, in1, in2, in3, in4, in5, in6, in7, out, sel
  Multiplexer #(.select(2), .enable("false")) multiplexer_44 ();  // open: in0, in1, in2, in3, out, sel
  Demultiplexer #(.select(1), .enable("false")) demultiplexer_40 ();  // open: out0, out1, in, sel
  Demultiplexer #(.select(3), .enable("false")) demultiplexer_41 ();  // open: out0, out1, out2, out3, out4, out5, out6, out7, in, sel
  Demultiplexer #(.select(2), .enable("false")) demultiplexer_42 ();  // open: out0, out1, out2, out3, in, sel
  Decoder #(.select(1), .enable("false")) decoder_43 ();  // open: out0, out1, sel
  Decoder #(.select(3), .enable("false")) decoder_44 ();  // open: out0, out1, out2, out3, out4, out5, out6, out7, sel
  // Priority_Encoder #(.select(1)) priority_encoder_10: pin names not known
  Clock clock_3 ();  // open: out
  Clock clock_4 ();  // open: out
  Divider #(.width(8)) divider_1 ();  // open: a, b, out, upper, rem
  RAM #(.bus("asynch"), .addrWidth(5), .dataWidth(32)) ram_3 ();  // open: addr, data, sel, ld, clr
  // AND_Gate and_59 is placed but not wired
  // AND_Gate and_60 is placed but not wired
  // AND_Gate and_61 is placed but not wired
  // NAND_Gate nand_55 is placed but not wired
  // NAND_Gate nand_56 is placed but not wired
  // NAND_Gate nand_57 is placed but not wired
  // OR_Gate or_59 is placed but not wired
  // OR_Gate or_60 is placed but not wired
  // OR_Gate or_61 is placed but not wired
  // XOR_Gate xor_55 is placed but not wired
  // XOR_Gate xor_56 is placed but not wired
  // XOR_Gate xor_57 is placed but not wired
  // XNOR_Gate xnor_58 is placed but not wired
  // XNOR_Gate xnor_59 is placed but not wired
  // XNOR_Gate xnor_60 is placed but not wired
  // Odd_Parity odd_parity_55 is placed but not wired
  // Odd_Parity odd_parity_56 is placed but not wired
  // Odd_Parity odd_parity_57 is placed but not wired
  // NOT_Gate not_7 is placed but not wired
  // XNOR_Gate xnor_61 is placed but not wired
  Multiplexer #(.select(3), .enable("true")) multiplexer_45 ();  // open: in0, in1, in2, in3, in4, in5, in6, in7, out, sel, en
  Multiplexer #(.select(2), .enable("true")) multiplexer_46 ();  // open: in0, in1, in2, in3, out, sel, en
  Demultiplexer #(.select(1), .enable("true")) demultiplexer_43 ();  // open: out0, out1, in, sel, en
  Demultiplexer #(.select(3), .enable("true")) demultiplexer_44 ();  // open: out0, out1, out2, out3, out4, out5, out6, out7, in, sel, en
  Demultiplexer #(.select(2), .enable("true")) demultiplexer_45 ();  // open: out0, out1, out2, out3, in, sel, en
  Decoder #(.select(1), .enable("true")) decoder_45 ();  // open: out0, out1, sel, en
  Decoder #(.select(3), .enable("true")) decoder_46 ();  // open: out0, out1, out2, out3, out4, out5, out6, out7, sel, en
  // Priority_Encoder #(.select(2)) priority_encoder_11: pin names not known
  Negator #(.width(8)) negator_1 ();  // open: in, out
  Keyboard keyboard_1 ();  // open: clk, re, clr, avail, data
  // AND_Gate and_62 is placed but not wired
  // AND_Gate and_63 is placed but not wired
  // AND_Gate and_64 is placed but not wired
  // NAND_Gate nand_58 is placed but not wired
  // NAND_Gate nand_59 is placed but not wired
  // NAND_Gate nand_60 is placed but not wired
  // OR_Gate or_62 is placed but not wired
  // OR_Gate or_63 is placed but not wired
  // OR_Gate or_64 is placed but not wired
  // XOR_Gate xor_58 is placed but not wired
  // XOR_Gate xor_59 is placed but not wired
  // XOR_Gate xor_60 is placed but not wired
  // XNOR_Gate xnor_62 is placed but not wired
  // XNOR_Gate xnor_63 is placed but not wired
  // XNOR_Gate xnor_64 is placed but not wired
  // Odd_Parity odd_parity_58 is placed but not wired
  // Odd_Parity odd_parity_59 is placed but not wired
  // Odd_Parity odd_parity_60 is placed but not wired
  Controlled_Inverter controlled_inverter_16 ();  // open: in, out, en
  // NOT_Gate not_8 is placed but not wired
  Multiplexer #(.select(3), .enable("false")) multiplexer_47 ();  // open: in0, in1, in2, in3, in4, in5, in6, in7, out, sel
  Multiplexer #(.select(2), .enable("false")) multiplexer_48 ();  // open: in0, in1, in2, in3, out, sel
  Demultiplexer #(.select(1), .enable("false")) demultiplexer_46 ();  // open: out0, out1, in, sel
  Demultiplexer #(.select(3), .enable("false")) demultiplexer_47 ();  // open: out0, out1, out2, out3, out4, out5, out6, out7, in, sel
  Demultiplexer #(.select(2), .enable("false")) demultiplexer_48 ();  // open: out0, out1, out2, out3, in, sel
  Decoder #(.select(1), .enable("false")) decoder_47 ();  // open: out0, out1, sel
  Decoder #(.select(3), .enable("false")) decoder_48 ();  // open: out0, out1, out2, out3, out4, out5, out6, out7, sel
  // Priority_Encoder #(.select(3)) priority_encoder_12: pin names not known
  Comparator #(.width(8)) comparator_1 ();  // open: a, b, gt, eq, lt
  TTY tty_1 ();  // open: data, clk, we, clr
endmodule

module sub (
  input  in_1,
  input  in_2,
  input  in_3,
  output out_4
);
endmodule

module plain (
  input  in_1,
  input  in_2,
  input  in_3,
  input  in_4,
  input  in_5,
  output out_6,
  output out_7
);
endmodule
