// Logisim project every-part.circ as structural Verilog: 1 circuit, main circuit main
module main (
  input  in_1
);

  // Probe on nothing
  Pull_Resistor pull_resistor_1 ();  // open: node
  Clock clock_1 ();  // open: out
  Transistor transistor_1 ();  // open: in, out, gate
  // Transmission_Gate transmission_1: pin names not known; wires that end beside it: 1'b1, 1'b0
  Bit_Extender bit_extender_1 ();  // open: in, out
  // NOT_Gate not_1 is placed but not wired
  // Buffer buffer_1 is placed but not wired
  // AND_Gate and_1 is placed but not wired
  // OR_Gate or_1 is placed but not wired
  // NAND_Gate nand_1 is placed but not wired
  // NOR_Gate nor_1 is placed but not wired
  // XOR_Gate xor_1 is placed but not wired
  // XNOR_Gate xnor_1 is placed but not wired
  // Odd_Parity odd_parity_1 is placed but not wired
  // Even_Parity even_parity_1 is placed but not wired
  Controlled_Buffer controlled_buffer_1 ();  // open: in, out, en
  Controlled_Inverter controlled_inverter_1 ();  // open: in, out, en
  Multiplexer multiplexer_1 ();  // open: in0, in1, out, sel, en
  Demultiplexer demultiplexer_1 ();  // open: out0, out1, in, sel, en
  Decoder decoder_1 ();  // open: out0, out1, sel, en
  Priority_Encoder priority_encoder_1 ();  // open: in0, in1, in2, in3, in4, in5, in6, in7, out, en_in, gs, en_out
  BitSelector bitselector_1 ();  // open: in, out, sel
  Adder adder_1 ();  // open: a, b, out, cin, cout
  Subtractor subtractor_1 ();  // open: a, b, out, bin, bout
  Multiplier multiplier_1 ();  // open: a, b, out, cin, cout
  Divider divider_1 ();  // open: a, b, out, upper, rem
  Negator negator_1 ();  // open: in, out
  Comparator comparator_1 ();  // open: a, b, gt, eq, lt
  Shifter shifter_1 ();  // open: in, dist, out
  BitAdder bitadder_1 ();  // open: in0, out
  BitFinder bitfinder_1 ();  // open: in, index, found
  D_Flip_Flop d_ff_1 ();  // open: clk, D, Q, Qn, preset, en, reset
  T_Flip_Flop t_ff_1 ();  // open: clk, T, Q, Qn, preset, reset, en
  J_K_Flip_Flop j_k_ff_1 ();  // open: J, clk, K, Q, Qn, preset, en, reset
  S_R_Flip_Flop s_r_ff_1 ();  // open: S, clk, R, Q, Qn, preset, reset, en
  Register register_1 ();  // open: D, en, Q, clk, clr
  Counter counter_1 ();  // open: load, D, count, Q, carry, clk, clr
  Shift_Register shift_register_1 ();  // open: shift, in, clk, out, load, clr, d0, q0, d1, q1, d2, q2, d3, q3, d4, q4, d5, q5, d6, q6, d7, q7
  Random random_1 ();  // open: clk, next, out, clr
  RAM ram_1 ();  // open: addr, data, sel, clk, ld, clr
  ROM rom_1 ();  // open: addr, data, sel
  Button button_1 ();  // open: out
  Joystick joystick_1 ();  // open: x, y
  Keyboard keyboard_1 ();  // open: clk, re, clr, avail, data
  LED led_1 ();  // open: in
  _7_Segment_Display u_7_segment_display_1 ();  // open: g, f, a, b, e, d, c, dp
  Hex_Digit_Display hex_digit_display_1 ();  // open: value, dp
  DotMatrix dotmatrix_1 ();  // open: col0, col1, col2, col3, col4
  TTY tty_1 ();  // open: data, clk, we, clr
endmodule
