// Logisim project importer.circ as structural Verilog: 3 circuits, main circuit top
module top (
  input  A,
  input  B,
  output Y,
  output Z
);

  \nand  nand_1 (.a(A), .b(B), .y(Y));
  inverter inverter_1 (.in_1(A), .out_2(Z));
endmodule

module \nand  (
  input  a,
  input  b,
  output y
);

  wire and_1_out;

  and and_1 (and_1_out, a, b);
  inverter inverter_1 (.in_1(and_1_out), .out_2(y));
endmodule

// NOT
module inverter (
  input  in_1,
  output out_2
);

  not not_1 (out_2, in_1);
endmodule
