// Logisim project layout.circ as structural Verilog: 10 circuits, main circuit gate
module gate (
  input  in_1,
  input  in_2,
  output out_3
);

  and and_1 (out_3, in_1, in_2);
endmodule

module mux (
  input  in_1,
  input  in_2,
  input  in_3,
  output out_4
);

  Multiplexer #(.enable("false")) multiplexer_1 (.in0(in_2), .in1(in_3), .out(out_4), .sel(in_1));
endmodule

module splitters (
  input  [3:0] in_1,
  input  [3:0] in_2,
  input  [3:0] in_3,
  input  [3:0] in_4,
  output [1:0] out_5,
  output [1:0] out_6,
  output [1:0] out_7,
  output [1:0] out_8,
  output [1:0] out_9,
  output [1:0] out_10,
  output [1:0] out_11,
  output [1:0] out_12
);


  assign out_5 = in_1[1:0];
  assign out_6 = in_1[3:2];
  assign out_7 = in_2[1:0];
  assign out_8 = in_2[3:2];
  assign out_9 = in_3[1:0];
  assign out_10 = in_3[3:2];
  assign out_11 = in_4[3:2];
  assign out_12 = in_4[1:0];
endmodule

module tee (
  input  in_1,
  output out_2,
  output out_3
);

  not not_1 (out_2, in_1);
  not not_2 (out_3, in_1);
endmodule

module not_in_front (
  input  in_1,
  input  in_2,
  output out_3
);

  or or_1 (out_3, in_1, ~in_2);  // OR_Gate
endmodule

module texts (
);

  // Probe on nothing
  // Probe on nothing

  // Notes on the sheet:
  //   hola
endmodule

module junction (
  input  in_1,
  output out_2
);


  assign out_2 = in_1;
endmodule

module \instance  (
  input  in_1,
  output out_2
);

  inner inner_1 (.in_1(in_1), .out_2(out_2));
endmodule

module untidy (
  input  in_1,
  output out_2
);


  assign out_2 = in_1;
endmodule

module inner (
  input  in_1,
  output out_2
);
endmodule
