// Logisim project nets.circ as structural Verilog
module split (
  input  [3:0] in_1,
  output [1:0] out_2,
  output [1:0] out_3
);


  assign out_2 = in_1[1:0];
  assign out_3 = in_1[3:2];
endmodule

module \join  (
  input  [1:0] in_1,
  input  [1:0] in_2,
  output [3:0] out_3
);


  assign out_3 = {in_2, in_1};
endmodule

module both (
  input  [1:0] in_1,
  input  [3:0] in_2
);


  assign in_2[1:0] = in_1;
endmodule

module through_tunnels (
  input  [3:0] in_1,
  output [1:0] out_2
);


  assign out_2 = in_1[1:0];

  // Other names for the same wires on the sheet: x[3:0] = in_1
endmodule

module tunnels (
  input  in_1,
  input  in_2,
  input  in_3,
  output out_4,
  output out_5,
  output out_6,
  output out_7
);


  assign in_3 = in_2;
  assign out_4 = in_1;
  assign out_5 = in_2;
  assign out_7 = out_6;

  // Other names for the same wires on the sheet: a = in_1; b = in_2; c = out_6
endmodule

module lone_tunnels (
  output out_1
);


  // Other names for the same wires on the sheet: d = out_1
endmodule

module lacking (
  input  in_1
);

  RAM #(.bus("separate")) ram_1 (.ld(in_1));  // open: addr, din, data, str, sel, clk, clr
endmodule

module junction (
  input  in_1,
  output out_2
);


  assign out_2 = in_1;
endmodule
