// Logisim project reader-basics.circ as structural Verilog: 2 circuits, main circuit top
module half (
  input  in_1,
  output y
);
endmodule

module top (
);

  // AND_Gate and_1 is placed but not wired
  // OR_Gate or_1 is placed but not wired
  Multiplexer #(.width(32)) multiplexer_1 ();  // open: in0, in1, out, sel, en
  half half_1 ();  // open: in_1, y
  // Ghost ghost_1: pin names not known

  // Notes on the sheet:
  //   Hola
endmodule
