// Logisim project subcircuits.circ as structural Verilog: 3 circuits, main circuit top
module top (
);

  middle middle_1 ();  // open: a, y
  leaf leaf_1 ();  // open: in_1, in_2, out_3
endmodule

module middle (
  input  a,
  output [3:0] y
);

  leaf leaf_1 ();  // open: in_1, in_2, out_3
endmodule

// L
module leaf (
  input  in_1,
  input  in_2,
  output out_3
);
endmodule
